// Digital circuit ConventionalAlarmClock.dig as structural Verilog
module ConventionalAlarmClock (
  input  CLK,
  input  CLR,
  input  SETUP_TIME,
  input  MIN_ADV,
  input  HR_ADV,
  input  SETUP_ALARM,
  input  ALARM_EN,
  input  PlaceHolder,
  input  [13:0] PlaceHolder_14,
  input  [1:0] PlaceHolder_2,
  output [5:0] SECOND,
  output [5:0] MINUTES,
  output [4:0] HOURS,
  output [5:0] ALARM_MINUTES,
  output [4:0] ALARM_HOURS,
  output [13:0] SEG_SECONDS,
  output [13:0] SEG_MINUTES,
  output [13:0] SEG_HOURS,
  output BUZZ
);

  wire and_1_out, and_2_out, and_3_out, and_4_out, and_5_out, and_6_out, and_7_out, and_8_out,
       comparator_1_eq, comparator_2_eq, not_1_out, not_2_out, not_3_out, not_4_out;
  wire [13:0] sevensegmentdecoder_1_data_out, sevensegmentdecoder_2_data_out, sevensegmentdecoder_3_data_out,
       sevensegmentdecoder_4_data_out, sevensegmentdecoder_5_data_out;

  not not_1 (not_1_out, SETUP_ALARM);
  and and_1 (and_1_out, and_3_out, MIN_ADV);
  and and_2 (and_2_out, and_3_out, HR_ADV);
  and and_3 (and_3_out, not_1_out, SETUP_TIME);
  not not_2 (not_2_out, SETUP_TIME);
  and and_4 (and_4_out, not_2_out, SETUP_ALARM);
  not not_3 (not_3_out, CLR);
  and and_5 (and_5_out, CLK, not_3_out);
  and and_6 (and_6_out, MIN_ADV, and_4_out);
  and and_7 (and_7_out, HR_ADV, and_4_out);
  BabylonianClock babylonianclock_1 (
    .CLK(and_5_out), .CLR(CLR), .SETUP(and_3_out), .MIN_ADV(and_1_out), .HR_ADV(and_2_out), .SECONDS(SECOND),
    .MINUTES(MINUTES), .HOURS(HOURS));
  BabylonianAlarm babylonianalarm_1 (
    .CLR(CLR), .SETUP(and_4_out), .MIN_ADV(and_6_out), .HR_ADV(and_7_out), .MINUTES(ALARM_MINUTES),
    .HOURS(ALARM_HOURS));
  SevenSegmentDecoder sevensegmentdecoder_1 (
    .DATA_IN({PlaceHolder, SECOND}), .DATA_OUT(sevensegmentdecoder_1_data_out));
  SevenSegmentDecoder sevensegmentdecoder_2 (
    .DATA_IN({PlaceHolder, MINUTES}), .DATA_OUT(sevensegmentdecoder_2_data_out));
  SevenSegmentDecoder sevensegmentdecoder_3 (
    .DATA_IN({PlaceHolder_2, HOURS}), .DATA_OUT(sevensegmentdecoder_3_data_out));
  SevenSegmentDecoder sevensegmentdecoder_4 (
    .DATA_IN({PlaceHolder, ALARM_MINUTES}), .DATA_OUT(sevensegmentdecoder_4_data_out));
  SevenSegmentDecoder sevensegmentdecoder_5 (
    .DATA_IN({PlaceHolder_2, ALARM_HOURS}), .DATA_OUT(sevensegmentdecoder_5_data_out));
  Multiplexer #(.Bits(14)) multiplexer_1 (
    .sel(SETUP_ALARM), .in_0(sevensegmentdecoder_1_data_out), .in_1(PlaceHolder_14), .out(SEG_SECONDS));
  Multiplexer #(.Bits(14)) multiplexer_2 (
    .sel(SETUP_ALARM), .in_0(sevensegmentdecoder_2_data_out), .in_1(sevensegmentdecoder_4_data_out),
    .out(SEG_MINUTES));
  Multiplexer #(.Bits(14)) multiplexer_3 (
    .sel(SETUP_ALARM), .in_0(sevensegmentdecoder_3_data_out), .in_1(sevensegmentdecoder_5_data_out),
    .out(SEG_HOURS));
  Comparator #(.Bits(14)) comparator_1 (
    .a(sevensegmentdecoder_2_data_out), .b(sevensegmentdecoder_4_data_out), .eq(comparator_1_eq));  // open: gt, lt
  Comparator #(.Bits(14)) comparator_2 (
    .a(sevensegmentdecoder_3_data_out), .b(sevensegmentdecoder_5_data_out), .eq(comparator_2_eq));  // open: gt, lt
  and and_8 (and_8_out, comparator_1_eq, comparator_2_eq);
  not not_4 (not_4_out, ALARM_EN);
  and and_9 (BUZZ, and_8_out, not_4_out);

  // Notes on the sheet:
  //   CLK: Hz: 10
endmodule
