// Digital circuit FrenchRepublicanCalendar.dig as structural Verilog
module FrenchRepublicanCalendar (
  input  CLK,
  input  CLR,
  input  SETUP,
  input  MIN_ADV,
  input  HR_ADV,
  input  Day_ADV,
  input  WEEK_ADV,
  input  Month_ADV,
  output [6:0] SECONDS,
  output [6:0] MINUTES,
  output [3:0] HOURS,
  output [3:0] DAYS,
  output [1:0] WEEKS,
  output [3:0] MONTHS,
  output [3:0] YEARS
);

  wire and_1_out, and_2_out, and_3_out, and_4_out, and_5_out, and_6_out, and_7_out, and_8_out, and_9_out,
       and_10_out, and_11_out, and_12_out, and_13_out, and_14_out, and_15_out, and_16_out, and_17_out,
       and_18_out, and_19_out, not_1_out, not_2_out, not_3_out, not_4_out, not_5_out, not_6_out, not_7_out,
       not_8_out, not_9_out, not_10_out, not_11_out, not_12_out, not_13_out, or_1_out, or_2_out, or_3_out,
       or_4_out, or_5_out, or_6_out, or_7_out, or_8_out, or_9_out, or_10_out, or_11_out, or_12_out,
       or_13_out, or_14_out;

  and and_1 (and_1_out, ~SETUP, CLK);  // And
  or or_1 (or_1_out, and_1_out, CLR);
  or or_2 (or_2_out, CLR, and_2_out);
  Counter #(.Bits(7)) SECONDS_COUNTER (.en(1'b1), .C(or_1_out), .clr(or_2_out), .out(SECONDS));  // open: ovf
  and and_2 (and_2_out, SECONDS[0], SECONDS[1], not_3_out, not_2_out, not_1_out, SECONDS[5], SECONDS[6]);
  and and_3 (and_3_out, ~and_1_out, and_2_out);  // And
  not not_1 (not_1_out, SECONDS[4]);
  not not_2 (not_2_out, SECONDS[3]);
  not not_3 (not_3_out, SECONDS[2]);
  or or_3 (or_3_out, and_4_out, and_3_out, CLR);
  or or_4 (or_4_out, CLR, and_5_out);
  and and_4 (and_4_out, MIN_ADV, SETUP);
  Counter #(.Bits(7)) MINUTES_COUNTER (.en(1'b1), .C(or_3_out), .clr(or_4_out), .out(MINUTES));  // open: ovf
  and and_5 (and_5_out, MINUTES[0], MINUTES[1], not_6_out, not_5_out, not_4_out, MINUTES[5], MINUTES[6]);
  and and_6 (and_6_out, ~or_3_out, and_5_out);  // And
  not not_4 (not_4_out, MINUTES[4]);
  not not_5 (not_5_out, MINUTES[3]);
  not not_6 (not_6_out, MINUTES[2]);
  and and_7 (and_7_out, HR_ADV, SETUP);
  or or_5 (or_5_out, and_7_out, and_6_out, CLR);
  or or_6 (or_6_out, CLR, and_8_out);
  Counter #(.Bits(4)) HOURS_COUNTER (.en(1'b1), .C(or_5_out), .clr(or_6_out), .out(HOURS));  // open: ovf
  and and_8 (and_8_out, HOURS[0], not_8_out, not_7_out, HOURS[3]);
  and and_9 (and_9_out, ~or_5_out, and_8_out);  // And
  not not_7 (not_7_out, HOURS[2]);
  not not_8 (not_8_out, HOURS[1]);
  and and_10 (and_10_out, Day_ADV, SETUP);
  or or_7 (or_7_out, and_10_out, and_9_out, CLR);
  or or_8 (or_8_out, CLR, and_11_out);
  Counter #(.Bits(4)) DAYS_COUNTER (.en(1'b1), .C(or_7_out), .clr(or_8_out), .out(DAYS));  // open: ovf
  and and_11 (and_11_out, DAYS[0], not_10_out, not_9_out, DAYS[3]);
  and and_12 (and_12_out, ~or_7_out, and_11_out);  // And
  not not_9 (not_9_out, DAYS[2]);
  not not_10 (not_10_out, DAYS[1]);
  and and_13 (and_13_out, WEEK_ADV, SETUP);
  or or_9 (or_9_out, and_13_out, and_12_out, CLR);
  or or_10 (or_10_out, CLR, and_14_out);
  Counter #(.Bits(2)) WEEKS_COUNTER (.en(1'b1), .C(or_9_out), .clr(or_10_out), .out(WEEKS));  // open: ovf
  and and_14 (and_14_out, not_11_out, WEEKS[1]);
  and and_15 (and_15_out, ~or_9_out, and_14_out);  // And
  not not_11 (not_11_out, WEEKS[0]);
  and and_16 (and_16_out, Month_ADV, SETUP);
  or or_11 (or_11_out, and_16_out, and_15_out, CLR);
  or or_12 (or_12_out, CLR, and_17_out);
  Counter #(.Bits(4)) MONTHS_COUNTER (.en(1'b1), .C(or_11_out), .clr(or_12_out), .out(MONTHS));  // open: ovf
  and and_17 (and_17_out, MONTHS[0], MONTHS[1], not_12_out, MONTHS[3]);
  and and_18 (and_18_out, ~or_11_out, and_17_out);  // And
  not not_12 (not_12_out, MONTHS[2]);
  or or_13 (or_13_out, and_18_out, CLR);
  or or_14 (or_14_out, CLR, and_19_out);
  Counter #(.Bits(4)) HOURSYEAR (.en(1'b1), .C(or_13_out), .clr(or_14_out), .out(YEARS));  // open: ovf
  and and_19 (and_19_out, YEARS[0], YEARS[1], not_13_out, YEARS[3]);
  not not_13 (not_13_out, YEARS[2]);

  // Notes on the sheet:
  //   CLK: Hz: 2147483647
endmodule
