// Digital circuit FrenchRepublicanCalendarAlarm.dig as structural Verilog
module FrenchRepublicanCalendarAlarm (
  input  CLR,
  input  SETUP,
  input  MIN_ADV,
  input  HR_ADV,
  input  DAY_ADV,
  input  WEEK_ADV,
  input  MONTH_ADV,
  output [6:0] MINUTES,
  output [3:0] HOURS,
  output [3:0] DAYS,
  output [1:0] WEEKS,
  output [3:0] MONTHS
);

  wire and_1_out, and_2_out, and_3_out, and_4_out, and_5_out, and_6_out, and_7_out, and_8_out, and_9_out,
       and_10_out, not_1_out, not_2_out, not_3_out, not_4_out, not_5_out, not_6_out, not_7_out, not_8_out,
       not_9_out, not_10_out, or_1_out, or_2_out, or_3_out, or_4_out, or_5_out, or_6_out, or_7_out, or_8_out,
       or_9_out, or_10_out;

  and and_1 (and_1_out, MIN_ADV, SETUP);
  or or_1 (or_1_out, and_1_out, CLR);
  or or_2 (or_2_out, CLR, and_2_out);
  Counter #(.Bits(7)) MINUTES_COUNTER (.en(1'b1), .C(or_1_out), .clr(or_2_out), .out(MINUTES));  // open: ovf
  and and_2 (and_2_out, MINUTES[0], MINUTES[1], not_3_out, not_2_out, not_1_out, MINUTES[5], MINUTES[6]);
  not not_1 (not_1_out, MINUTES[4]);
  not not_2 (not_2_out, MINUTES[3]);
  not not_3 (not_3_out, MINUTES[2]);
  or or_3 (or_3_out, CLR, and_4_out);
  and and_3 (and_3_out, HR_ADV, SETUP);
  or or_4 (or_4_out, and_3_out, CLR);
  Counter #(.Bits(4)) HOURS_COUNTER (.en(1'b1), .C(or_4_out), .clr(or_3_out), .out(HOURS));  // open: ovf
  and and_4 (and_4_out, HOURS[0], not_5_out, not_4_out, HOURS[3]);
  not not_4 (not_4_out, HOURS[2]);
  not not_5 (not_5_out, HOURS[1]);
  and and_5 (and_5_out, DAY_ADV, SETUP);
  or or_5 (or_5_out, and_5_out, CLR);
  or or_6 (or_6_out, CLR, and_6_out);
  Counter #(.Bits(4)) DAYS_COUNTER (.en(1'b1), .C(or_5_out), .clr(or_6_out), .out(DAYS));  // open: ovf
  and and_6 (and_6_out, DAYS[0], not_7_out, not_6_out, DAYS[3]);
  not not_6 (not_6_out, DAYS[2]);
  not not_7 (not_7_out, DAYS[1]);
  or or_7 (or_7_out, and_7_out, CLR);
  or or_8 (or_8_out, CLR, and_8_out);
  and and_7 (and_7_out, WEEK_ADV, SETUP);
  Counter #(.Bits(2)) WEEKS_COUNTER (.en(1'b1), .C(or_7_out), .clr(or_8_out), .out(WEEKS));  // open: ovf
  and and_8 (and_8_out, not_8_out, WEEKS[1]);
  not not_8 (not_8_out, WEEKS[0]);
  and and_9 (and_9_out, MONTH_ADV, SETUP);
  or or_9 (or_9_out, and_9_out, CLR);
  or or_10 (or_10_out, CLR, and_10_out);
  Counter #(.Bits(4)) MONTHS_COUNTER (.en(1'b1), .C(or_9_out), .clr(or_10_out), .out(MONTHS));  // open: ovf
  and and_10 (and_10_out, MONTHS[0], not_10_out, not_9_out, MONTHS[3]);
  not not_9 (not_9_out, MONTHS[2]);
  not not_10 (not_10_out, MONTHS[1]);
endmodule
