// Digital circuit FrenchRepublicanCalendarAlarmClock.dig as structural Verilog
module FrenchRepublicanCalendarAlarmClock (
  input  CLK,
  input  CLR,
  input  SETUP_TIME,
  input  MIN_ADV,
  input  HR_ADV,
  input  SETUP_ALARM,
  input  ALARM_EN,
  input  [13:0] PlaceHolder_14,
  input  [2:0] PlaceHolder_2,
  input  [2:0] PlaceHolder_15,
  input  DAY_ADV,
  input  WEEK_ADV,
  input  MONTH_ADV,
  input  [2:0] PlaceHolder_16,
  input  [4:0] PlaceHolder_17,
  input  [2:0] PlaceHolder_18,
  input  [2:0] PlaceHolder_19,
  input  [2:0] PlaceHolder_20,
  input  [4:0] PlaceHolder_21,
  input  [2:0] PlaceHolder_22,
  input  [13:0] PlaceHolder_23,
  output [6:0] SECOND,
  output [6:0] MINUTES,
  output [3:0] HOURS,
  output [6:0] ALARM_MINUTES,
  output [3:0] ALARM_HOURS,
  output [13:0] SEG_SECONDS,
  output [13:0] SEG_MINUTES,
  output [13:0] SEG_HOURS,
  output BUZZ,
  output [3:0] DAYS,
  output [1:0] WEEKS,
  output [3:0] MONTHS,
  output [3:0] YEARS,
  output [13:0] SEG_DAYS,
  output [13:0] SEG_WEEKS,
  output [13:0] SEG_MONTHS,
  output [13:0] SEG_YEARS,
  output [3:0] ALARM_DAYS,
  output [1:0] ALARM_WEEKS,
  output [3:0] ALARM_MONTHS
);

  wire and_1_out, and_2_out, and_3_out, and_4_out, and_5_out, and_6_out, and_7_out, and_8_out, and_9_out,
       and_10_out, and_11_out, and_12_out, and_13_out, and_14_out, comparator_1_eq, comparator_2_eq,
       comparator_3_eq, comparator_4_eq, comparator_5_eq, not_1_out, not_2_out, not_3_out, not_4_out;
  wire [13:0] sevensegmentdecoder_1_data_out, sevensegmentdecoder_2_data_out, sevensegmentdecoder_3_data_out,
       sevensegmentdecoder_4_data_out, sevensegmentdecoder_5_data_out, sevensegmentdecoder_6_data_out,
       sevensegmentdecoder_7_data_out, sevensegmentdecoder_8_data_out, sevensegmentdecoder_9_data_out,
       sevensegmentdecoder_10_data_out, sevensegmentdecoder_11_data_out, sevensegmentdecoder_12_data_out;

  not not_1 (not_1_out, SETUP_ALARM);
  and and_1 (and_1_out, not_1_out, SETUP_TIME);
  and and_2 (and_2_out, and_1_out, MIN_ADV);
  and and_3 (and_3_out, and_1_out, HR_ADV);
  and and_4 (and_4_out, and_1_out, DAY_ADV);
  and and_5 (and_5_out, and_1_out, WEEK_ADV);
  and and_6 (and_6_out, and_1_out, MONTH_ADV);
  not not_2 (not_2_out, SETUP_TIME);
  and and_7 (and_7_out, not_2_out, SETUP_ALARM);
  not not_3 (not_3_out, CLR);
  and and_8 (and_8_out, CLK, not_3_out);
  and and_9 (and_9_out, MIN_ADV, and_7_out);
  and and_10 (and_10_out, HR_ADV, and_7_out);
  and and_11 (and_11_out, DAY_ADV, and_7_out);
  and and_12 (and_12_out, WEEK_ADV, and_7_out);
  and and_13 (and_13_out, MONTH_ADV, and_7_out);
  FrenchRepublicanCalendar frenchrepublicancalendar_1 (
    .CLK(and_8_out), .CLR(CLR), .SETUP(and_1_out), .MIN_ADV(and_2_out), .HR_ADV(and_3_out),
    .Day_ADV(and_4_out), .WEEK_ADV(and_5_out), .Month_ADV(and_6_out), .SECONDS(SECOND), .MINUTES(MINUTES),
    .HOURS(HOURS), .DAYS(DAYS), .WEEKS(WEEKS), .MONTHS(MONTHS), .YEARS(YEARS));
  FrenchRepublicanCalendarAlarm frenchrepublicancalendaralarm_1 (
    .CLR(CLR), .SETUP(and_7_out), .MIN_ADV(and_9_out), .HR_ADV(and_10_out), .DAY_ADV(and_11_out),
    .WEEK_ADV(and_12_out), .MONTH_ADV(and_13_out), .MINUTES(ALARM_MINUTES), .HOURS(ALARM_HOURS),
    .DAYS(ALARM_DAYS), .WEEKS(ALARM_WEEKS), .MONTHS(ALARM_MONTHS));
  SevenSegmentDecoder sevensegmentdecoder_1 (.DATA_IN(SECOND), .DATA_OUT(sevensegmentdecoder_1_data_out));
  SevenSegmentDecoder sevensegmentdecoder_2 (.DATA_IN(MINUTES), .DATA_OUT(sevensegmentdecoder_2_data_out));
  SevenSegmentDecoder sevensegmentdecoder_3 (
    .DATA_IN({PlaceHolder_2, HOURS}), .DATA_OUT(sevensegmentdecoder_3_data_out));
  SevenSegmentDecoder sevensegmentdecoder_4 (
    .DATA_IN({PlaceHolder_16, DAYS}), .DATA_OUT(sevensegmentdecoder_4_data_out));
  SevenSegmentDecoder sevensegmentdecoder_5 (
    .DATA_IN({PlaceHolder_17, WEEKS}), .DATA_OUT(sevensegmentdecoder_5_data_out));
  SevenSegmentDecoder sevensegmentdecoder_6 (
    .DATA_IN({PlaceHolder_18, MONTHS}), .DATA_OUT(sevensegmentdecoder_6_data_out));
  SevenSegmentDecoder sevensegmentdecoder_7 (
    .DATA_IN({PlaceHolder_19, YEARS}), .DATA_OUT(sevensegmentdecoder_7_data_out));
  SevenSegmentDecoder sevensegmentdecoder_8 (.DATA_IN(ALARM_MINUTES), .DATA_OUT(sevensegmentdecoder_8_data_out));
  SevenSegmentDecoder sevensegmentdecoder_9 (
    .DATA_IN({PlaceHolder_15, ALARM_HOURS}), .DATA_OUT(sevensegmentdecoder_9_data_out));
  SevenSegmentDecoder sevensegmentdecoder_10 (
    .DATA_IN({PlaceHolder_20, ALARM_DAYS}), .DATA_OUT(sevensegmentdecoder_10_data_out));
  SevenSegmentDecoder sevensegmentdecoder_11 (
    .DATA_IN({PlaceHolder_21, ALARM_WEEKS}), .DATA_OUT(sevensegmentdecoder_11_data_out));
  SevenSegmentDecoder sevensegmentdecoder_12 (
    .DATA_IN({PlaceHolder_22, ALARM_MONTHS}), .DATA_OUT(sevensegmentdecoder_12_data_out));
  Multiplexer #(.Bits(14)) multiplexer_1 (
    .sel(SETUP_ALARM), .in_0(sevensegmentdecoder_1_data_out), .in_1(PlaceHolder_14), .out(SEG_SECONDS));
  Multiplexer #(.Bits(14)) multiplexer_2 (
    .sel(SETUP_ALARM), .in_0(sevensegmentdecoder_2_data_out), .in_1(sevensegmentdecoder_8_data_out),
    .out(SEG_MINUTES));
  Multiplexer #(.Bits(14)) multiplexer_3 (
    .sel(SETUP_ALARM), .in_0(sevensegmentdecoder_3_data_out), .in_1(sevensegmentdecoder_9_data_out),
    .out(SEG_HOURS));
  Multiplexer #(.Bits(14)) multiplexer_4 (
    .sel(SETUP_ALARM), .in_0(sevensegmentdecoder_4_data_out), .in_1(sevensegmentdecoder_10_data_out),
    .out(SEG_DAYS));
  Multiplexer #(.Bits(14)) multiplexer_5 (
    .sel(SETUP_ALARM), .in_0(sevensegmentdecoder_5_data_out), .in_1(sevensegmentdecoder_11_data_out),
    .out(SEG_WEEKS));
  Multiplexer #(.Bits(14)) multiplexer_6 (
    .sel(SETUP_ALARM), .in_0(sevensegmentdecoder_6_data_out), .in_1(sevensegmentdecoder_12_data_out),
    .out(SEG_MONTHS));
  Multiplexer #(.Bits(14)) multiplexer_7 (
    .sel(SETUP_ALARM), .in_0(sevensegmentdecoder_7_data_out), .in_1(PlaceHolder_23), .out(SEG_YEARS));
  Comparator #(.Bits(14)) comparator_1 (
    .a(sevensegmentdecoder_2_data_out), .b(sevensegmentdecoder_8_data_out), .eq(comparator_1_eq));  // open: gt, lt
  Comparator #(.Bits(14)) comparator_2 (
    .a(sevensegmentdecoder_3_data_out), .b(sevensegmentdecoder_9_data_out), .eq(comparator_2_eq));  // open: gt, lt
  Comparator #(.Bits(14)) comparator_3 (
    .a(sevensegmentdecoder_4_data_out), .b(sevensegmentdecoder_10_data_out), .eq(comparator_3_eq));  // open: gt, lt
  Comparator #(.Bits(14)) comparator_4 (
    .a(sevensegmentdecoder_5_data_out), .b(sevensegmentdecoder_11_data_out), .eq(comparator_4_eq));  // open: gt, lt
  Comparator #(.Bits(14)) comparator_5 (
    .a(sevensegmentdecoder_6_data_out), .b(sevensegmentdecoder_12_data_out), .eq(comparator_5_eq));  // open: gt, lt
  and and_14 (and_14_out, comparator_1_eq, comparator_2_eq, comparator_3_eq, comparator_4_eq, comparator_5_eq);
  not not_4 (not_4_out, ALARM_EN);
  and and_15 (BUZZ, and_14_out, not_4_out);
endmodule
