// Digital circuit FrenchRepublicanalarm.dig as structural Verilog
module FrenchRepublicanalarm (
  input  CLR,
  input  SETUP,
  input  MIN_ADV,
  input  HR_ADV,
  output [6:0] MINUTES,
  output [3:0] HOURS
);

  wire and_1_out, and_2_out, and_3_out, and_4_out, not_1_out, not_2_out, not_3_out, not_4_out, not_5_out,
       or_1_out, or_2_out, or_3_out, or_4_out;

  or or_1 (or_1_out, CLR, and_2_out);
  and and_1 (and_1_out, MIN_ADV, SETUP);
  or or_2 (or_2_out, and_1_out, CLR);
  Counter #(.Bits(7)) MINUTES_COUNTER (.en(1'b1), .C(or_2_out), .clr(or_1_out), .out(MINUTES));  // open: ovf
  and and_2 (and_2_out, MINUTES[0], MINUTES[1], not_3_out, not_2_out, not_1_out, MINUTES[5], MINUTES[6]);
  not not_1 (not_1_out, MINUTES[4]);
  not not_2 (not_2_out, MINUTES[3]);
  not not_3 (not_3_out, MINUTES[2]);
  and and_3 (and_3_out, HR_ADV, SETUP);
  or or_3 (or_3_out, and_3_out, CLR);
  or or_4 (or_4_out, CLR, and_4_out);
  Counter #(.Bits(4)) HOURS_COUNTER (.en(1'b1), .C(or_3_out), .clr(or_4_out), .out(HOURS));  // open: ovf
  and and_4 (and_4_out, HOURS[0], not_5_out, not_4_out, HOURS[3]);
  not not_4 (not_4_out, HOURS[2]);
  not not_5 (not_5_out, HOURS[1]);
endmodule
