// Digital circuit FrenchRepublicanlogic.dig as structural Verilog
module FrenchRepublicanlogic (
  input  CLK,
  input  CLR,
  input  SETUP,
  input  MIN_ADV,
  input  HR_ADV,
  output [6:0] SECONDS,
  output [6:0] MINUTES,
  output [3:0] HOURS
);

  wire and_1_out, and_2_out, and_3_out, and_4_out, and_5_out, and_6_out, and_7_out, and_8_out, not_1_out,
       not_2_out, not_3_out, not_4_out, not_5_out, not_6_out, not_7_out, not_8_out, or_1_out, or_2_out,
       or_3_out, or_4_out, or_5_out, or_6_out;

  and and_1 (and_1_out, ~SETUP, CLK);  // And
  or or_1 (or_1_out, and_1_out, CLR);
  or or_2 (or_2_out, CLR, and_2_out);
  Counter #(.Bits(7)) SECONDS_COUNTER (.en(1'b1), .C(or_1_out), .clr(or_2_out), .out(SECONDS));  // open: ovf
  and and_2 (and_2_out, SECONDS[0], SECONDS[1], not_3_out, not_2_out, not_1_out, SECONDS[5], SECONDS[6]);
  and and_3 (and_3_out, ~and_1_out, and_2_out);  // And
  not not_1 (not_1_out, SECONDS[4]);
  not not_2 (not_2_out, SECONDS[3]);
  not not_3 (not_3_out, SECONDS[2]);
  and and_4 (and_4_out, MIN_ADV, SETUP);
  or or_3 (or_3_out, and_4_out, and_3_out, CLR);
  or or_4 (or_4_out, CLR, and_5_out);
  Counter #(.Bits(7)) MINUTES_COUNTER (.en(1'b1), .C(or_3_out), .clr(or_4_out), .out(MINUTES));  // open: ovf
  and and_5 (and_5_out, MINUTES[0], MINUTES[1], not_6_out, not_5_out, not_4_out, MINUTES[5], MINUTES[6]);
  and and_6 (and_6_out, ~or_3_out, and_5_out);  // And
  not not_4 (not_4_out, MINUTES[4]);
  not not_5 (not_5_out, MINUTES[3]);
  not not_6 (not_6_out, MINUTES[2]);
  and and_7 (and_7_out, HR_ADV, SETUP);
  or or_5 (or_5_out, and_7_out, and_6_out, CLR);
  or or_6 (or_6_out, CLR, and_8_out);
  Counter #(.Bits(4)) HOURS_COUNTER (.en(1'b1), .C(or_5_out), .clr(or_6_out), .out(HOURS));  // open: ovf
  and and_8 (and_8_out, HOURS[0], not_8_out, not_7_out, HOURS[3]);
  not not_7 (not_7_out, HOURS[2]);
  not not_8 (not_8_out, HOURS[1]);

  // Notes on the sheet:
  //   CLK: Hz: 500
endmodule
