// Digital circuit SevenSegmentDecoder.dig as structural Verilog
module SevenSegmentDecoder (
  input  [6:0] DATA_IN,
  output [13:0] DATA_OUT
);

  LookUpTable #(.Bits(14)) lookuptable_1 (
    .in0(DATA_IN[0]), .in1(DATA_IN[1]), .in2(DATA_IN[2]), .in3(DATA_IN[3]), .in4(DATA_IN[4]),
    .in5(DATA_IN[5]), .in6(DATA_IN[6]), .out(DATA_OUT));

  // Notes on the sheet:
  //   contents of lookuptable_1 (hex, n*v repeats v):
  //   3f7e,3f30,3f6d,3f79,3f33,3f5b,3f5f,3f70,3f7f,3f7b,187e,1830,186d,1879,1833,185b,185f,1870,187f,
  //   187b,36fe,36b0,36ed,36f9,36b3,36db,36df,36f0,36ff,36fb,3cfe,3cb0,3ced,3cf9,3cb3,3cdb,3cdf,3cf0,
  //   3cff,3cfb,19fe,19b0,19ed,19f9,19b3,19db,19df,19f0,19ff,19fb,2dfe,2db0,2ded,2df9,2db3,2ddb,2ddf,
  //   2df0,2dff,2dfb,2ffe,2fb0,2fed,2ff9,2fb3,2fdb,2fdf,2ff0,2fff,2ffb,387e,3830,386d,3879,3833,385b,
  //   385f,3870,387f,387b,3ffe,3fb0,3fed,3ff9,3fb3,3fdb,3fdf,3ff0,3fff,3ffb,3dfe,3db0,3ded,3df9,3db3,
  //   3ddb,3ddf,3df0,3dff,3dfb
endmodule
