// Digital circuit Shifter.dig as structural Verilog
module Shifter (
  input  CLK,
  input  CLR,
  input  LOAD,
  input  SHIFT,
  input  SHIFT_IN,
  input  [12:0] DATA_IN,
  output [12:0] DATA_OUT
);

  ShiftBit shiftbit_1 (
    .EN(SHIFT), .SHIFT_IN(SHIFT_IN), .LOAD(LOAD), .BIT_IN(DATA_IN[12]), .CLR(CLR), .CLK(CLK),
    .OUT(DATA_OUT[12]));
  ShiftBit shiftbit_2 (
    .EN(SHIFT), .SHIFT_IN(DATA_OUT[12]), .LOAD(LOAD), .BIT_IN(DATA_IN[11]), .CLR(CLR), .CLK(CLK),
    .OUT(DATA_OUT[11]));
  ShiftBit shiftbit_3 (
    .EN(SHIFT), .SHIFT_IN(DATA_OUT[11]), .LOAD(LOAD), .BIT_IN(DATA_IN[10]), .CLR(CLR), .CLK(CLK),
    .OUT(DATA_OUT[10]));
  ShiftBit shiftbit_4 (
    .EN(SHIFT), .SHIFT_IN(DATA_OUT[10]), .LOAD(LOAD), .BIT_IN(DATA_IN[9]), .CLR(CLR), .CLK(CLK),
    .OUT(DATA_OUT[9]));
  ShiftBit shiftbit_5 (
    .EN(SHIFT), .SHIFT_IN(DATA_OUT[9]), .LOAD(LOAD), .BIT_IN(DATA_IN[8]), .CLR(CLR), .CLK(CLK),
    .OUT(DATA_OUT[8]));
  ShiftBit shiftbit_6 (
    .EN(SHIFT), .SHIFT_IN(DATA_OUT[8]), .LOAD(LOAD), .BIT_IN(DATA_IN[7]), .CLR(CLR), .CLK(CLK),
    .OUT(DATA_OUT[7]));
  ShiftBit shiftbit_7 (
    .EN(SHIFT), .SHIFT_IN(DATA_OUT[7]), .LOAD(LOAD), .BIT_IN(DATA_IN[6]), .CLR(CLR), .CLK(CLK),
    .OUT(DATA_OUT[6]));
  ShiftBit shiftbit_8 (
    .EN(SHIFT), .SHIFT_IN(DATA_OUT[6]), .LOAD(LOAD), .BIT_IN(DATA_IN[5]), .CLR(CLR), .CLK(CLK),
    .OUT(DATA_OUT[5]));
  ShiftBit shiftbit_9 (
    .EN(SHIFT), .SHIFT_IN(DATA_OUT[5]), .LOAD(LOAD), .BIT_IN(DATA_IN[4]), .CLR(CLR), .CLK(CLK),
    .OUT(DATA_OUT[4]));
  ShiftBit shiftbit_10 (
    .EN(SHIFT), .SHIFT_IN(DATA_OUT[4]), .LOAD(LOAD), .BIT_IN(DATA_IN[3]), .CLR(CLR), .CLK(CLK),
    .OUT(DATA_OUT[3]));
  ShiftBit shiftbit_11 (
    .EN(SHIFT), .SHIFT_IN(DATA_OUT[3]), .LOAD(LOAD), .BIT_IN(DATA_IN[2]), .CLR(CLR), .CLK(CLK),
    .OUT(DATA_OUT[2]));
  ShiftBit shiftbit_12 (
    .EN(SHIFT), .SHIFT_IN(DATA_OUT[2]), .LOAD(LOAD), .BIT_IN(DATA_IN[1]), .CLR(CLR), .CLK(CLK),
    .OUT(DATA_OUT[1]));
  ShiftBit shiftbit_13 (
    .EN(SHIFT), .SHIFT_IN(DATA_OUT[1]), .LOAD(LOAD), .BIT_IN(DATA_IN[0]), .CLR(CLR), .CLK(CLK),
    .OUT(DATA_OUT[0]));
endmodule
